# Fritzing sketch Esquema proyecto (saved by Fritzing 1.0.4)
breadboards: 1

parts:
  Componente2 = Bluetooth Module Breakout - Roving Networks (RN-41)
  LED1 = LED - 5mm [color="Red (633nm)" current=0.030A package="5 mm [THT]"]
  Keypad4x1 = Keypad Membran 4x4
  Componente3 = Arduino Uno (Rev3)
  M1 = Dagu DGServo 9g (Top view) [part_number=RS001B]
  J1 = Piezo Speaker
  R1 = Resistor [tolerance=±5% power=0.25W resistance=220 package=THT]
  LED2 = LED - 5mm [color="Red (633nm)" current=0.030A package="5 mm [THT]"]
  R2 = Resistor [tolerance=±5% power=0.25W resistance=220 package=THT]
  R3 = Resistor [tolerance=±5% power=0.25W resistance=220 package=THT]
  R4 = Resistor [tolerance=±5% power=0.25W resistance=220 package=THT]
  R5 = Resistor [tolerance=±5% power=0.25W resistance=220 package=THT]
  R6 = Resistor [tolerance=±5% power=0.25W resistance=220 package=THT]
  Componente4 = HC-SR501 Body Sensor Module

nets:
  VCC: Componente2.VCC, Componente3.5V, M1.vcc, R3.Pin_1, R4.Pin_1, R5.Pin_1, R6.Pin_1, Componente4.OUT
  GND: Componente2.GND, LED1.anode, Componente3.GND, M1.gnd, J1.pin1, LED2.anode, Componente4.GND
  N1: Componente2.UARTTX, Componente3.D0/RX
  N2: Componente2.UARTRX, Componente3.D1/TX
  N3: LED1.cathode, R1.Pin_0
  N4: Keypad4x1.Pin1, Componente3.D5_PWM
  N5: Keypad4x1.Pin2, Componente3.D6_PWM
  N6: Keypad4x1.Pin3, Componente3.D7
  N7: Keypad4x1.Pin5, Componente3.A3, R6.Pin_0
  N8: Keypad4x1.Pin6, Componente3.A2, R5.Pin_0
  N9: Keypad4x1.Pin7, Componente3.A1, R4.Pin_0
  N10: Keypad4x1.Pin8, Componente3.A0, R3.Pin_0
  N11: Componente3.A4/SDA, R1.Pin_1
  N12: Componente3.D2, M1.pulse
  N13: Componente3.D3_PWM, J1.pin2
  N14: Componente3.D4, Componente4.VCC
  N15: LED2.cathode, R2.Pin_0

custom parts:
  Keypad Membran 4x4: Membrane Keypad 4x4 Matrix
  HC-SR501 Body Sensor Module: Pyroelectric Infrared PIR Motion Sensor Detector Module
